// Logisim project 8bitcomputer.circ as structural Verilog: 13 circuits, main circuit main
module main (
  input  in_1,
  input  in_2
);

  wire Ce_prime, clk, Cp, Cp_t, Ea, Ei_prime, Ep, Eu, La_prime, Lb_prime, Li_prime, Lm_prime, Lo_prime,
       n7segmentdisplay_1_a, n7segmentdisplay_1_b, n7segmentdisplay_1_c, n7segmentdisplay_1_d,
       n7segmentdisplay_1_e, n7segmentdisplay_1_f, n7segmentdisplay_1_g, n7segmentdisplay_2_a,
       n7segmentdisplay_2_b, n7segmentdisplay_2_c, n7segmentdisplay_2_d, n7segmentdisplay_2_e,
       n7segmentdisplay_2_f, n7segmentdisplay_2_g, not_1_out, not_2_out, not_3_out, not_4_out, not_5_out,
       not_6_out, not_7_out, Su;
  wire [3:0] controlled_buffer_2_out, IR_q, IR_q_2, MAR_q;
  wire [7:0] accumulator_q, ALU_output, controlled_buffer_3_out, controlled_buffer_5_out,
       controlled_buffer_8_out, controlled_buffer_9_out, output_register_q, program_counter_output,
       ram_1_data, reg_B_q;
  wire [7:4] controlled_buffer_2_out_2;

  Clock clock_1 (.out(clk));
  Register #(.width(4)) MAR (.D(controlled_buffer_2_out), .Q(MAR_q), .clk(clk));  // open: en, clr
  not not_1 (not_1_out, Ce_prime);
  program_counter program_counter (.clk(clk), .clr(in_1), .Cp(Cp_t), .\output (program_counter_output));
  RAM #(.addrWidth(4)) ram_1 (.addr(MAR_q), .data(ram_1_data), .sel(not_1_out));  // open: clk, ld, clr
  Register IR (.D(controlled_buffer_3_out), .Q({IR_q, IR_q_2}), .clk(clk), .clr(in_1));  // open: en
  control_unit control_unit (
    .clk(clk), .set(in_2), .clr(in_1), .IR_CU(IR_q),
    .out_5({Cp, Ep, Lm_prime, Ce_prime, Li_prime, Ei_prime, La_prime, Ea, Su, Eu, Lb_prime, Lo_prime}));
  assign ram_1_data = Ep ? program_counter_output : 8'bz;  // Controlled_Buffer controlled_buffer_1
  not not_2 (not_2_out, Lm_prime);
  assign {controlled_buffer_2_out_2, controlled_buffer_2_out} = not_2_out ? ram_1_data : 8'bz;  // Controlled_Buffer controlled_buffer_2
  not not_3 (not_3_out, Li_prime);
  assign controlled_buffer_3_out = not_3_out ? ram_1_data : 8'bz;  // Controlled_Buffer controlled_buffer_3
  assign ram_1_data = not_4_out ? {4'b0000, IR_q_2} : 8'bz;  // Controlled_Buffer controlled_buffer_4
  not not_4 (not_4_out, Ei_prime);
  assign controlled_buffer_5_out = not_5_out ? ram_1_data : 8'bz;  // Controlled_Buffer controlled_buffer_5
  not not_5 (not_5_out, La_prime);
  assign ram_1_data = Ea ? accumulator_q : 8'bz;  // Controlled_Buffer controlled_buffer_6
  assign ram_1_data = Eu ? ALU_output : 8'bz;  // Controlled_Buffer controlled_buffer_7
  assign controlled_buffer_8_out = not_6_out ? ram_1_data : 8'bz;  // Controlled_Buffer controlled_buffer_8
  not not_6 (not_6_out, Lb_prime);
  not not_7 (not_7_out, Lo_prime);
  assign controlled_buffer_9_out = not_7_out ? ram_1_data : 8'bz;  // Controlled_Buffer controlled_buffer_9
  Register accumulator (.D(controlled_buffer_5_out), .Q(accumulator_q), .clk(clk), .clr(in_1));  // open: en
  ALU ALU (.reg_A(accumulator_q), .Su(Su), .reg_B(reg_B_q), .\output (ALU_output));
  Register reg_B (.D(controlled_buffer_8_out), .Q(reg_B_q), .clk(clk), .clr(in_1));  // open: en
  _7_Segment_Display u_7_segment_display_1 (
    .g(n7segmentdisplay_1_g), .f(n7segmentdisplay_1_f), .a(n7segmentdisplay_1_a), .b(n7segmentdisplay_1_b),
    .e(n7segmentdisplay_1_e), .d(n7segmentdisplay_1_d), .c(n7segmentdisplay_1_c));  // open: dp
  Register output_register (.D(controlled_buffer_9_out), .Q(output_register_q), .clk(clk), .clr(in_1));  // open: en
  _7segmentdisplay u_7segmentdisplay_1 (
    .B0(output_register_q[4]), .B1(output_register_q[5]), .B2(output_register_q[6]),
    .B3(output_register_q[7]), .a(n7segmentdisplay_1_a), .b(n7segmentdisplay_1_b), .c(n7segmentdisplay_1_c),
    .d(n7segmentdisplay_1_d), .e(n7segmentdisplay_1_e), .f(n7segmentdisplay_1_f), .g(n7segmentdisplay_1_g));
  _7_Segment_Display u_7_segment_display_2 (
    .g(n7segmentdisplay_2_g), .f(n7segmentdisplay_2_f), .a(n7segmentdisplay_2_a), .b(n7segmentdisplay_2_b),
    .e(n7segmentdisplay_2_e), .d(n7segmentdisplay_2_d), .c(n7segmentdisplay_2_c));  // open: dp
  _7segmentdisplay u_7segmentdisplay_2 (
    .B0(output_register_q[0]), .B1(output_register_q[1]), .B2(output_register_q[2]),
    .B3(output_register_q[3]), .a(n7segmentdisplay_2_a), .b(n7segmentdisplay_2_b), .c(n7segmentdisplay_2_c),
    .d(n7segmentdisplay_2_d), .e(n7segmentdisplay_2_e), .f(n7segmentdisplay_2_f), .g(n7segmentdisplay_2_g));

  // Other names for the same wires on the sheet: clr = in_1; set = in_2

  // Notes on the sheet:
  //   RAM
  //   Output interface
endmodule

module ring_counter (
  input  clk,
  input  set,
  input  clr,
  output out_4,
  output out_5,
  output out_6,
  output out_7,
  output out_8,
  output out_9
);

  D_Flip_Flop d_ff_1 (.clk(clk), .D(out_9), .Q(out_4), .preset(set), .reset(clr));  // open: Qn, en
  D_Flip_Flop d_ff_2 (.clk(clk), .D(out_4), .Q(out_5), .reset(clr));  // open: Qn, preset, en
  D_Flip_Flop d_ff_3 (.clk(clk), .D(out_5), .Q(out_6), .reset(clr));  // open: Qn, preset, en
  D_Flip_Flop d_ff_4 (.clk(clk), .D(out_6), .Q(out_7), .reset(clr));  // open: Qn, preset, en
  D_Flip_Flop d_ff_5 (.clk(clk), .D(out_7), .Q(out_8), .reset(clr));  // open: Qn, preset, en
  D_Flip_Flop d_ff_6 (.clk(clk), .D(out_8), .Q(out_9), .reset(clr));  // open: Qn, preset, en
endmodule

module control_unit (
  input  clk,
  input  set,
  input  clr,
  input  [3:0] IR_CU,
  output [11:0] out_5
);

  wire nor_1_out, ring_counter_1_out_4, ring_counter_1_out_5, ring_counter_1_out_6, ring_counter_1_out_7,
       ring_counter_1_out_8, ring_counter_1_out_9;
  wire [3:0] adder_1_out, adder_2_out, controlled_buffer_1_out, rom_1_data;

  ring_counter ring_counter_1 (
    .clk(clk), .set(set), .clr(clr), .out_4(ring_counter_1_out_4), .out_5(ring_counter_1_out_5),
    .out_6(ring_counter_1_out_6), .out_7(ring_counter_1_out_7), .out_8(ring_counter_1_out_8),
    .out_9(ring_counter_1_out_9));
  assign controlled_buffer_1_out = nor_1_out ? 4'b1111 : 4'bz;  // Controlled_Buffer controlled_buffer_1
  nor nor_1 (nor_1_out, ring_counter_1_out_4, ring_counter_1_out_5, ring_counter_1_out_6, ring_counter_1_out_7, ring_counter_1_out_8, ring_counter_1_out_9);
  assign controlled_buffer_1_out = ring_counter_1_out_4 ? 4'b0000 : 4'bz;  // Controlled_Buffer controlled_buffer_2
  assign controlled_buffer_1_out = ring_counter_1_out_5 ? 4'b0001 : 4'bz;  // Controlled_Buffer controlled_buffer_3
  assign controlled_buffer_1_out = ring_counter_1_out_6 ? 4'b0010 : 4'bz;  // Controlled_Buffer controlled_buffer_4
  assign controlled_buffer_1_out = ring_counter_1_out_7 ? rom_1_data : 4'bz;  // Controlled_Buffer controlled_buffer_5
  ROM #(.addrWidth(4), .dataWidth(4)) rom_1 (.addr(IR_CU), .data(rom_1_data));  // open: sel
  Adder #(.width(4)) adder_1 (.a(rom_1_data), .b(4'b0001), .out(adder_1_out));  // open: cin, cout
  assign controlled_buffer_1_out = ring_counter_1_out_8 ? adder_1_out : 4'bz;  // Controlled_Buffer controlled_buffer_6
  assign controlled_buffer_1_out = ring_counter_1_out_9 ? adder_2_out : 4'bz;  // Controlled_Buffer controlled_buffer_7
  Adder #(.width(4)) adder_2 (.a(rom_1_data), .b(4'b0010), .out(adder_2_out));  // open: cin, cout
  ROM #(.addrWidth(4), .dataWidth(12)) rom_2 (.addr(controlled_buffer_1_out), .data(out_5));  // open: sel

  // Notes on the sheet:
  //   ROM 1
  //   contents of rom_1 (hex, n*v repeats v):
  //   3 6 9 11*0 c
  //   ROM 2
  //   contents of rom_2 (hex, n*v repeats v):
  //   5e3 be3 263 1a3 2c3 3e3 1a3 2e1 3c7 1a3 2e1 3cf 3f2 3e3 3e3 fff
endmodule

module ALU (
  input  [7:0] reg_A,
  input  Su,
  input  [7:0] reg_B,
  output [7:0] \output 
);

  wire not_1_out;
  wire [7:0] adder_1_out, subtractor_1_out;

  Adder adder_1 (.a(reg_A), .b(reg_B), .out(adder_1_out));  // open: cin, cout
  Subtractor subtractor_1 (.a(reg_A), .b(reg_B), .out(subtractor_1_out));  // open: bin, bout
  assign \output  = not_1_out ? adder_1_out : 8'bz;  // Controlled_Buffer controlled_buffer_1
  not not_1 (not_1_out, Su);
  assign \output  = Su ? subtractor_1_out : 8'bz;  // Controlled_Buffer controlled_buffer_2
endmodule

module program_counter (
  input  clk,
  input  clr,
  input  Cp,
  output [7:0] \output 
);

  wire and_1_out, and_2_out;

  T_Flip_Flop t_ff_1 (.clk(clk), .T(1'b1), .Q(\output [0]), .reset(clr), .en(Cp));  // open: Qn, preset
  and and_1 (and_1_out, \output [0], \output [1]);
  T_Flip_Flop t_ff_2 (.clk(clk), .T(\output [0]), .Q(\output [1]), .reset(clr), .en(Cp));  // open: Qn, preset
  T_Flip_Flop t_ff_3 (.clk(clk), .T(and_1_out), .Q(\output [2]), .reset(clr), .en(Cp));  // open: Qn, preset
  and and_2 (and_2_out, and_1_out, \output [2]);
  T_Flip_Flop t_ff_4 (.clk(clk), .T(and_2_out), .Q(\output [3]), .reset(clr), .en(Cp));  // open: Qn, preset
endmodule

module SA (
  input  B3,
  input  B2,
  input  B1,
  input  B0,
  output a
);

  wire and_1_out, and_2_out, and_3_out, and_4_out, and_5_out, and_6_out, not_1_out, not_2_out, not_3_out,
       not_4_out, not_5_out, not_6_out, not_7_out;

  not not_1 (not_1_out, B2);
  not not_2 (not_2_out, B0);
  not not_3 (not_3_out, B3);
  not not_4 (not_4_out, B3);
  not not_5 (not_5_out, B2);
  not not_6 (not_6_out, B1);
  not not_7 (not_7_out, B0);
  and and_1 (and_1_out, not_1_out, not_2_out);
  and and_2 (and_2_out, not_3_out, B1);
  and and_3 (and_3_out, not_4_out, B2, B0);
  and and_4 (and_4_out, B2, B1);
  and and_5 (and_5_out, B3, not_5_out, not_6_out);
  and and_6 (and_6_out, B3, not_7_out);
  or or_1 (a, and_1_out, and_2_out, and_3_out, and_4_out, and_5_out, and_6_out);
endmodule

module SB (
  input  B3,
  input  B2,
  input  B1,
  input  B0,
  output b
);

  wire and_1_out, and_2_out, and_3_out, and_4_out, and_5_out, and_6_out, not_1_out, not_2_out, not_3_out,
       not_4_out, not_5_out, not_6_out, not_7_out, not_8_out, not_9_out, not_10_out, not_11_out;

  not not_1 (not_1_out, B3);
  and and_1 (and_1_out, not_1_out, not_2_out);
  not not_2 (not_2_out, B2);
  not not_3 (not_3_out, B3);
  and and_2 (and_2_out, not_3_out, not_4_out, not_5_out);
  not not_4 (not_4_out, B1);
  not not_5 (not_5_out, B0);
  not not_6 (not_6_out, B2);
  and and_3 (and_3_out, not_6_out, not_7_out);
  not not_7 (not_7_out, B1);
  not not_8 (not_8_out, B2);
  and and_4 (and_4_out, not_8_out, not_9_out);
  not not_9 (not_9_out, B0);
  not not_10 (not_10_out, B3);
  and and_5 (and_5_out, not_10_out, B1, B0);
  and and_6 (and_6_out, B3, not_11_out, B0);
  not not_11 (not_11_out, B1);
  or or_1 (b, and_1_out, and_2_out, and_3_out, and_4_out, and_5_out, and_6_out);
endmodule

module SC (
  input  B3,
  input  B2,
  input  B1,
  input  B0,
  output c
);

  wire and_1_out, and_2_out, and_3_out, and_4_out, and_5_out, not_1_out, not_2_out, not_3_out, not_4_out,
       not_5_out, not_6_out;

  not not_1 (not_1_out, B3);
  not not_2 (not_2_out, B1);
  not not_3 (not_3_out, B3);
  not not_4 (not_4_out, B1);
  not not_5 (not_5_out, B3);
  not not_6 (not_6_out, B2);
  and and_1 (and_1_out, not_1_out, not_2_out);
  and and_2 (and_2_out, not_3_out, B0);
  and and_3 (and_3_out, not_4_out, B0);
  and and_4 (and_4_out, not_5_out, B2);
  and and_5 (and_5_out, B3, not_6_out);
  or or_1 (c, and_1_out, and_2_out, and_3_out, and_4_out, and_5_out);
endmodule

module SD (
  input  B3,
  input  B2,
  input  B1,
  input  B0,
  output d
);

  wire and_1_out, and_2_out, and_3_out, and_4_out, and_5_out, not_1_out, not_2_out, not_3_out, not_4_out,
       not_5_out, not_6_out, not_7_out;

  not not_1 (not_1_out, B3);
  not not_2 (not_2_out, B2);
  not not_3 (not_3_out, B0);
  not not_4 (not_4_out, B2);
  not not_5 (not_5_out, B1);
  not not_6 (not_6_out, B0);
  not not_7 (not_7_out, B1);
  and and_1 (and_1_out, not_1_out, not_2_out, not_3_out);
  and and_2 (and_2_out, not_4_out, B1, B0);
  and and_3 (and_3_out, B2, not_5_out, B0);
  and and_4 (and_4_out, B2, B1, not_6_out);
  and and_5 (and_5_out, B3, not_7_out);
  or or_1 (d, and_1_out, and_2_out, and_3_out, and_4_out, and_5_out);
endmodule

module SE (
  input  B3,
  input  B2,
  input  B1,
  input  B0,
  output e
);

  wire and_1_out, and_2_out, and_3_out, and_4_out, not_1_out, not_2_out, not_3_out;

  not not_1 (not_1_out, B2);
  not not_2 (not_2_out, B0);
  not not_3 (not_3_out, B0);
  and and_1 (and_1_out, not_1_out, not_2_out);
  and and_2 (and_2_out, B1, not_3_out);
  and and_3 (and_3_out, B3, B1);
  and and_4 (and_4_out, B3, B2);
  or or_1 (e, and_1_out, and_2_out, and_3_out, and_4_out);
endmodule

module SF (
  input  B3,
  input  B2,
  input  B1,
  input  B0,
  output f
);

  wire and_1_out, and_2_out, and_3_out, and_4_out, and_5_out, not_1_out, not_2_out, not_3_out, not_4_out,
       not_5_out, not_6_out;

  not not_1 (not_1_out, B1);
  not not_2 (not_2_out, B0);
  not not_3 (not_3_out, B3);
  not not_4 (not_4_out, B1);
  not not_5 (not_5_out, B0);
  not not_6 (not_6_out, B2);
  and and_1 (and_1_out, not_1_out, not_2_out);
  and and_2 (and_2_out, not_3_out, B2, not_4_out);
  and and_3 (and_3_out, B2, not_5_out);
  and and_4 (and_4_out, B3, not_6_out);
  and and_5 (and_5_out, B3, B1);
  or or_1 (f, and_1_out, and_2_out, and_3_out, and_4_out, and_5_out);
endmodule

module SG (
  input  B3,
  input  B2,
  input  B1,
  input  B0,
  output g
);

  wire and_1_out, and_2_out, and_3_out, and_4_out, and_5_out, not_1_out, not_2_out, not_3_out, not_4_out,
       not_5_out;

  not not_1 (not_1_out, B2);
  not not_2 (not_2_out, B0);
  not not_3 (not_3_out, B3);
  not not_4 (not_4_out, B1);
  not not_5 (not_5_out, B2);
  and and_1 (and_1_out, not_1_out, B1);
  and and_2 (and_2_out, B1, not_2_out);
  and and_3 (and_3_out, not_3_out, B2, not_4_out);
  and and_4 (and_4_out, B3, not_5_out);
  and and_5 (and_5_out, B3, B0);
  or or_1 (g, and_1_out, and_2_out, and_3_out, and_4_out, and_5_out);
endmodule

module _7segmentdisplay (
  input  B0,
  input  B1,
  input  B2,
  input  B3,
  output a,
  output b,
  output c,
  output d,
  output e,
  output f,
  output g
);

  SA segment_A (.B3(B3), .B2(B2), .B1(B1), .B0(B0), .a(a));
  SB segment_B (.B3(B3), .B2(B2), .B1(B1), .B0(B0), .b(b));
  SC segment_C (.B3(B3), .B2(B2), .B1(B1), .B0(B0), .c(c));
  SD segment_D (.B3(B3), .B2(B2), .B1(B1), .B0(B0), .d(d));
  SE segment_E (.B3(B3), .B2(B2), .B1(B1), .B0(B0), .e(e));
  SF segment_F (.B3(B3), .B2(B2), .B1(B1), .B0(B0), .f(f));
  SG segment_G (.B3(B3), .B2(B2), .B1(B1), .B0(B0), .g(g));
endmodule
